# Fritzing sketch diagram (saved by Fritzing 0.9.3b)
breadboards: 1

parts:
  U1 = 74HC595 [package="DIP16 [THT]"]
  U2 = 74HC595 [package="DIP16 [THT]"]
  LED1 = LED - 5mm [color="Red (633nm)" package="5 mm [THT]"]
  LED2 = LED - 5mm [color="Red (633nm)" package="5 mm [THT]"]
  LED3 = LED - 5mm [color="Red (633nm)" package="5 mm [THT]"]
  LED4 = LED - 5mm [color="Red (633nm)" package="5 mm [THT]"]
  LED5 = LED - 5mm [color="Red (633nm)" package="5 mm [THT]"]
  LED6 = LED - 5mm [color="Red (633nm)" package="5 mm [THT]"]
  LED7 = LED - 5mm [color="Red (633nm)" package="5 mm [THT]"]
  LED8 = LED - 5mm [color="Red (633nm)" package="5 mm [THT]"]
  LED9 = LED - 5mm [color="Red (633nm)" package="5 mm [THT]"]
  LED10 = LED - 5mm [color="Red (633nm)" package="5 mm [THT]"]
  LED11 = LED - 5mm [color="Red (633nm)" package="5 mm [THT]"]
  LED12 = LED - 5mm [color="Red (633nm)" package="5 mm [THT]"]
  LED13 = LED - 5mm [color="Red (633nm)" package="5 mm [THT]"]
  LED14 = LED - 5mm [color="Red (633nm)" package="5 mm [THT]"]
  LED15 = LED - 5mm [color="Red (633nm)" package="5 mm [THT]"]
  LED16 = LED - 5mm [color="Red (633nm)" package="5 mm [THT]"]
  Part1 = Arduino Uno (Rev3)

nets:
  N1: U1.Q1, LED2.anode
  N2: U1.Q2, LED3.anode
  N3: U1.Q3, LED4.anode
  N4: U1.Q4, LED5.anode
  N5: U1.Q5, LED6.anode
  N6: U1.Q6, LED7.anode
  N7: U1.Q7, LED8.anode
  GND: U1.GND, U1.OE, U2.GND, U2.OE, LED1.cathode, LED2.cathode, LED3.cathode, LED4.cathode, LED5.cathode, LED6.cathode, LED7.cathode, LED8.cathode, LED9.cathode, LED10.cathode, LED11.cathode, LED12.cathode, LED13.cathode, LED14.cathode, LED15.cathode, LED16.cathode, Part1.GND
  N8: U1.Q7', U2.DS
  VCC: U1.MR, U1.VCC, U2.MR, U2.VCC, Part1.5V
  N9: U1.SH_CP, U2.SH_CP, Part1.D11_PWM/MOSI
  N10: U1.ST_CP, U2.ST_CP, Part1.D12/MISO
  N11: U1.DS, Part1.D3_PWM
  N12: U1.Q0, LED1.anode
  N13: U2.Q1, LED10.anode
  N14: U2.Q2, LED11.anode
  N15: U2.Q3, LED12.anode
  N16: U2.Q4, LED13.anode
  N17: U2.Q5, LED14.anode
  N18: U2.Q6, LED15.anode
  N19: U2.Q7, LED16.anode
  N20: U2.Q0, LED9.anode
